# Fritzing sketch CaeliACO2.V05BME (saved by Fritzing 0.9.4)
circuit board: 7.99775cm x 6.45515cm
breadboards: 1

parts:
  MHZ19C-CM1106 = MH-Z19 CO2 sensor [part_number=MH-Z19]
  LED_R = LED - 5mm [color="Red (633nm)" package="5 mm [THT]"]
  LED_Y = LED - 5mm [color="Orange (605nm)" package="5 mm [THT]"]
  LED_G = LED - 5mm [color="Green (560nm)" package="5 mm [THT]"]
  R4-10K = Resistor [tolerance=±5% resistance=10k package=THT]
  R1-220 = Resistor [tolerance=±5% resistance=220 package=THT]
  R2-220 = Resistor [tolerance=±5% resistance=220 package=THT]
  R3-220 = Resistor [tolerance=±5% resistance=220 package=THT]
  SSD1306_64x128 = OLED 0.96" 128x64 I2C SSD1306 (GND/VCC)
  S1 = Pushbutton [package="[THT]"]
  DHT11 = Humidity and Temperature Sensor DHT11
  R5-10K = Resistor [tolerance=±5% resistance=10k package=THT]
  BME_280-5V = GY-BMEP280 Barometric Pressure Sensor - Breakout
  IC1 = IC, SIP package, 19 pins [chip_label=IC]
  U1 = ESP32-38PinWide [part_number=ESP32-38PinWide]

nets:
  N1: MHZ19C-CM1106.RX, U1.GPIO18
  N2: MHZ19C-CM1106.TX, U1.GPIO19
  VIN: MHZ19C-CM1106.Vin, R4-10K.Pin_1, DHT11.Vcc, R5-10K.Pin_1, BME_280-5V.VCC, IC1.pin1, U1.VIN
  GND: MHZ19C-CM1106.GND, R1-220.Pin_0, R2-220.Pin_0, R3-220.Pin_0, SSD1306_64x128.GND, S1.Pin_1, S1.Pin_2, DHT11.GND_1, DHT11.GND_2, BME_280-5V.GND, IC1.pin6, U1.GND
  N3: LED_R.cathode, R3-220.Pin_1
  N4: LED_R.anode, U1.GPIO15
  N5: LED_Y.cathode, R2-220.Pin_1
  N6: LED_Y.anode, U1.GPIO2
  N7: LED_G.cathode, R1-220.Pin_1
  N8: LED_G.anode, U1.GPIO0
  N9: R4-10K.Pin_0, S1.Pin_3, S1.Pin_4, U1.GPIO3
  N10: SSD1306_64x128.VCC, IC1.pin19, U1.3.3
  N11: SSD1306_64x128.SCL, BME_280-5V.SCL, U1.GPIO4
  N12: SSD1306_64x128.SCA, BME_280-5V.SDA, U1.GPIO5
  N13: DHT11.Data-signal, R5-10K.Pin_0, U1.GPIO23
  N14: IC1.pin2, U1.GPIO11
  N15: IC1.pin3, U1.GPIO10
  N16: IC1.pin4, U1.GPIO9
  N17: IC1.pin5, U1.GPIO13
  N18: IC1.pin7, U1.GPIO12
  N19: IC1.pin8, U1.GPIO14
  N20: IC1.pin9, U1.GPIO27
  N21: IC1.pin10, U1.GPIO26
  N22: IC1.pin11, U1.GPIO25
  N23: IC1.pin12, U1.GPIO33
  N24: IC1.pin13, U1.GPIO32
  N25: IC1.pin14, U1.GPIO35
  N26: IC1.pin15, U1.GPIO34
  N27: IC1.pin16, U1.GPIO39
  N28: IC1.pin17, U1.GPIO36
  N29: IC1.pin18, U1.EN

notes:
  CaeliA

custom parts:
  OLED 0.96" 128x64 I2C SSD1306 (GND/VCC): OLED 0.96" 128x64 I2C SSD1306 Pinout: GND/VCC/SCL/SDA
  Humidity and Temperature Sensor DHT11: Digital relative humidity & temperature sensor DHT11
  GY-BMEP280 Barometric Pressure Sensor - Breakout: The BME280 is a chip which was originally designed for the next generation of smartphones. It is made up of a very accurate pressure sensor and an associated temperature sensor which helps calibrate the pressure readings. And just for fun they threw in a pretty solid humidity sensor in there as well! So with an I2C connection you have access to enough weather data to make some pretty good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
  ESP32-38PinWide: Generic 38-Pin ESP32 with wide format (only access to one side of pins on a breadboard) based on Stephen Lilley's HiLetgo ESP-WROOM-32 ESP32 ESP-32S Development Board.
